# Fritzing sketch fritzing_sketch (saved by Fritzing 0.9.2b)

parts:
  Bauteil1 = Real Time Clock Module - DS1307 RTC Breakout Board
  Bauteil2 = Arduino Nano (Rev3.0)
  JQ6500 = JQ6500
  SP1 = SPEAKER [package=pcb_mount_speaker]
  0_01_µF = Capacitor [package=cap-pth-small2]
  0_33_µF = Capacitor [package=cap-pth-small2]
  VCC1 = Battery block 9V
  S1 = SWITCH-MOMENTARY-2 [package=reed_switch_pth]
  U1 = Voltage Regulator - 5V [package="TO220 [THT]"]
  part = LED - 5mm [color="Red (633nm)" package="5 mm [THT]"]
  LED2 = LED - 5mm [color="Red (633nm)" package="5 mm [THT]"]

nets:
  5V: Bauteil1.5V, Bauteil2.5V, JQ6500.VCC
  GND: Bauteil1.GND, Bauteil2.GND, JQ6500.GND, 0_01_µF.2, part.cathode, LED2.cathode
  N1: Bauteil1.SCL, Bauteil2.A5
  N2: Bauteil1.SDA, Bauteil2.A4
  N3: Bauteil2.D2, JQ6500.TX
  N4: Bauteil2.D3, JQ6500.RX
  N5: JQ6500.BUSY, part.anode, LED2.anode
  N6: JQ6500.SPK-, SP1.-
  N7: JQ6500.SPK+, SP1.+
  N8: 0_33_µF.1, S1.2, U1.input_voltage
  N9: 0_33_µF.2, VCC1.-, U1.GND
  N10: VCC1.+, S1.1

notes:
  AudioAdventcalendar, 1
